# Fritzing sketch Wiring Diagram TA Teknologi IoT (saved by Fritzing 0.9.3b)

parts:
  YL-83_-_Control_Board1 = YL-83 Rain Sensor - Control Board
  YL-83_-_Detection_Board1 = YL-83 Rain Sensor - Detection Board
  A1 = ESP32-S3-WROOM-1-N16R8 dev board
  DHT1 = Humidity and Temperature Sensor DHT11
  HC-SR04_Sensor_1 = HC-SR04 Ultrasonic Distance Sensor
  KY-1 = Keyes Hall Effect Sensor [package=THT]
  e-radionica_com1 = LM393 LDR breakout [part_number=100027]
  BATT1 = LiPoly Battery (1300mAh)
  J1 = Camdenboss CTB0158-12 [part_number=CTB0158-12 package=THT]
  J2 = Camdenboss CTB0158-12 [part_number=CTB0158-12 package=THT]
  F1 = Fan - Ventilador [package=THT]
  KY-3 = Keyes Relay [package=THT]
  KY-4 = Keyes Relay [package=THT]
  J3 = Basic Servo
  J4 = Piezo Speaker
  L2 = Solenoid
  Buck_Convertor1 = Buck Convertor [part_number=LM2596 package=THT]
  J5 = Camdenboss CTB0158-12 [part_number=CTB0158-12 package=THT]
  J6 = Camdenboss CTB0158-12 [part_number=CTB0158-12 package=THT]
  BULB2 = LEDs [package=led10mm]  # not connected
  BULB4 = LEDs [package=led10mm]  # not connected
  BULB1 = LEDs [package=led10mm]
  BULB3 = LEDs [package=led10mm]  # not connected
  KY-6 = Keyes Relay [package=THT]
  KY-7 = Keyes Relay [package=THT]

nets:
  N1: YL-83_-_Control_Board1.VCC, J2.terminal_8
  N2: YL-83_-_Control_Board1.GND, J1.terminal_8
  N3: YL-83_-_Control_Board1.AO, A1.Pin_32
  N4: YL-83_-_Control_Board1.POS, YL-83_-_Detection_Board1.POS
  N5: YL-83_-_Control_Board1.NEG, YL-83_-_Detection_Board1.NEG
  N6: A1.Pin_4, DHT1.Data-signal
  N7: A1.Pin_8, KY-1.signal
  N8: A1.Pin_9, e-radionica_com1.DO
  N9: A1.Pin_10, KY-3.signal
  N10: A1.Pin_11, KY-4.signal
  N11: A1.Pin_21, J2.terminal_1
  N12: A1.Pin_22, J1.terminal_1
  N13: A1.Pin_25, KY-7.signal
  N14: A1.Pin_26, KY-6.signal
  N15: A1.Pin_27, J3.pulse
  N16: A1.Pin_33, HC-SR04_Sensor_1.ECHO
  N17: A1.Pin_34, HC-SR04_Sensor_1.TRIG
  N18: DHT1.Vcc, J2.terminal_10
  N19: DHT1.GND_2, J1.terminal_10
  N20: HC-SR04_Sensor_1.VCC, J2.terminal_7
  N21: HC-SR04_Sensor_1.GND, J1.terminal_7
  N22: KY-1.ground, J1.terminal_9
  N23: KY-1.power, J2.terminal_9
  N24: e-radionica_com1.VCC, J2.terminal_11
  N25: e-radionica_com1.GND, J1.terminal_11
  N26: BATT1.positive, Buck_Convertor1.Positive_Input
  N27: BATT1.negative, Buck_Convertor1.Negative_Input, J6.terminal_1
  N28: J1.terminal_2, KY-6.ground
  N29: J1.terminal_3, KY-7.ground
  N30: J1.terminal_4, J3.gnd
  N31: J1.terminal_5, KY-3.ground
  N32: J1.terminal_6, KY-4.ground
  N33: J1.terminal_12, Buck_Convertor1.Negative_Output
  N34: J2.terminal_2, KY-6.power
  N35: J2.terminal_3, KY-7.power
  N36: J2.terminal_4, J3.vcc
  N37: J2.terminal_5, KY-3.power
  N38: J2.terminal_6, KY-4.power
  N39: J2.terminal_12, Buck_Convertor1.Positive_Output
  N40: F1.5V, KY-4.C
  N41: F1.GND, J6.terminal_3
  N42: KY-3.NC, J5.terminal_2
  N43: KY-3.C, BULB1.C
  N44: KY-4.NC, J5.terminal_3
  N45: J4.pin1, J6.terminal_4
  N46: J4.pin2, KY-7.C
  N47: L2.pin1, J6.terminal_5
  N48: L2.pin2, KY-6.C
  N49: J5.terminal_4, KY-7.NC
  N50: J5.terminal_5, KY-6.NC
  N51: J6.terminal_2, BULB1.A

notes:
  Source 5V
  Source 12V
  Buck Converter 12V to 5V
  Sensor LDR (Light Dependent Resistor)
  Sensor DHT11
  Sensor Hall Effect
  Rain sensor
  Sensor Ultrasonic
  ESP32-S3 N8R16
  Servo SG90
  Relay 1
  Relay 2
  Relay 3
  Relay 4
  Solenoid Door Lock
  Buzzer 12V
  Fan 12V
  LED 12V
  Battery

custom parts:
  YL-83 Rain Sensor - Control Board: The YL-83 is a rain sensor that has more resistance when dry and less resistance when wet. The module runs at 5V.
  YL-83 Rain Sensor - Detection Board: The YL-83 is a rain sensor that has more resistance when dry and less resistance when wet. The module runs at 5V.
  ESP32-S3-WROOM-1-N16R8 dev board: ESP32-S3 WIFI+BLE5.0 Development Board ESP32-S3-WROOM-1-N16R8(16M Flash/8SRAM).
  Humidity and Temperature Sensor DHT11: Digital relative humidity & temperature sensor DHT11
  Keyes Hall Effect Sensor: Keyes Magnetic Hall Effect Sensor Module for Arduino. Working voltage: 4.5V-25V.
  LiPoly Battery (1300mAh): Lithium Ion Polymer Battery (1300mAh)
  Fan - Ventilador: Ventilador de 2 pines, se encuentra comunmente en computadoras de escritorio
  Keyes Relay: The Keyes 5V relay module is suitable for SCM development, home appliance control. It uses a 5V~12V TIL control signal which can control DC / AC signal.
  Buck Convertor: DC to DC buck convertor
