# Fritzing sketch Wiring diagram Teknologi IoT (saved by Fritzing 0.9.3b)
breadboards: 4

parts:
  A1 = ESP32-S3-WROOM-1-N16R8 dev board [part_number="ESP32 Air Quality"]
  A2 = ESP32-S3-WROOM-1-N16R8 dev board [part_number="ESP32 S3 Water Quality"]
  A3 = ESP32-S3-WROOM-1-N16R8 dev board [part_number="ESP32 S3 Air Circulation"]
  A4 = ESP32-S3-WROOM-1-N16R8 dev board [part_number="ESP 32 S3 Automatic Pump"]
  Buck_Convertor1 = Buck Convertor [part_number=LM2596 package=THT]
  KY-1 = Keyes Relay [package=THT]
  KY-2 = Keyes Relay [package=THT]
  KY-3 = Keyes Relay [package=THT]
  F1 = Fan - Ventilador [package=THT]
  WATER_PUMP1 = water pump/motor  # not connected
  F2 = Fan - Ventilador [package=THT]
  Part3 = MQ-7 breakout
  M1 = PH meter with sensor in breadboard [package=THT]
  A5 = tds-sensor-meter-v1.0_1
  J1 = Basic Servo
  DHT1 = Humidity and Temperature Sensor DHT11
  HC-SR04_Sensor_1 = HC-SR04 Ultrasonic Distance Sensor
  A6 = Hanmatek HM305

nets:
  N1: A1.Pin_23, A1.Pin_24, A1.Pin_44
  N2: A2.Pin_1, A2.Pin_2
  N3: A2.Pin_22, A2.Pin_23, A2.Pin_24, A2.Pin_44
  N4: A2.Pin_27, J1.pulse
  N5: A2.Pin_40, M1.pin1
  N6: A2.Pin_41, A5.pin1
  N7: A3.Pin_1, A3.Pin_2, KY-2.power
  N8: A3.Pin_5, KY-2.signal
  N9: A3.Pin_10, DHT1.Data-signal
  N10: A3.Pin_22, A3.Pin_23, A3.Pin_24, A3.Pin_44, KY-2.ground
  N11: A4.Pin_1, A4.Pin_2, KY-3.power
  N12: A4.Pin_5, HC-SR04_Sensor_1.TRIG
  N13: A4.Pin_10, KY-3.signal
  N14: A4.Pin_12, HC-SR04_Sensor_1.ECHO
  N15: A4.Pin_22, A4.Pin_23, A4.Pin_24, A4.Pin_44, KY-3.ground
  N16: Buck_Convertor1.Negative_Input, A6.Pin_3
  VCC: Buck_Convertor1.Negative_Output, KY-3.NC, Part3.VCC, M1.pin2, A5.pin2, J1.vcc, DHT1.Vcc, HC-SR04_Sensor_1.VCC
  GND: Buck_Convertor1.Positive_Output, Part3.GND, M1.pin3, A5.pin3, J1.gnd, DHT1.GND_1, HC-SR04_Sensor_1.GND
  N17: KY-1.NC, F2.GND, A6.Pin_4
  N18: KY-1.C, F1.5V
  N19: KY-2.NC, F1.GND
  N20: KY-2.C, F2.5V

custom parts:
  ESP32-S3-WROOM-1-N16R8 dev board: ESP32-S3 WIFI+BLE5.0 Development Board ESP32-S3-WROOM-1-N16R8(16M Flash/8SRAM).
  Buck Convertor: DC to DC buck convertor
  Keyes Relay: The Keyes 5V relay module is suitable for SCM development, home appliance control. It uses a 5V~12V TIL control signal which can control DC / AC signal.
  Fan - Ventilador: Ventilador de 2 pines, se encuentra comunmente en computadoras de escritorio
  water pump/motor: WATER PUMP BY ARDUBLOCKTR
  MQ-7 breakout: SKU: 101282
  PH meter with sensor in breadboard: DFrobot PH meter (SKU SEN0161)
  : TDS Meter V1.0 Development Board Water Meter Filter Measuring Water Sensor Module.
  Humidity and Temperature Sensor DHT11: Digital relative humidity & temperature sensor DHT11
  Hanmatek HM305: DC Power Supply 30V5A HM305.
